# Fritzing sketch RFID_pn532andLockDoorSolenoid (saved by Fritzing 0.9.4)

parts:
  Part1 = Arduino Nano (Rev3.0) (ICSP)
  Part2 = Adafruit PN532 Breakout [part_number="Adafruit #364"]
  KY-1 = Keyes Relay [package=THT]
  Part3 = LCD1602-I2C
  JACK1 = 2.1mm Barrel Jack with Terminal Block [part_number="12 V"]

nets:
  N1: Part1.D9, KY-1.signal
  N2: Part1.D10, Part2.NSS/SCL/RX
  N3: Part1.D11/MOSI, Part2.MOSI/SDA/TX
  N4: Part1.D12/MISO, Part2.MISO
  N5: Part1.VIN, JACK1.POS
  5V: Part1.5V, Part2.+5.0V, Part3.VCC
  N6: Part1.A5, Part3.SCL
  N7: Part1.A4, Part3.SDA
  N8: Part1.D13/SCK, Part2.SCK
  GND: Part2.GND, KY-1.ground, Part3.GND, JACK1.NEG

notes:
  12V

custom parts:
  Adafruit PN532 Breakout: The PN532 is the most popular NFC chip, and is what is embedded in pretty much every phone or device that does NFC. It can pretty much do it all, such as read and write to tags and cards, communicate with phones (say for payment processing), and 'act' like a NFC tag. If you want to do any sort of embedded NFC work, this is the chip you'll want to use! NFC (Near Field Communications) is a way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
  Keyes Relay: The Keyes 5V relay module is suitable for SCM development, home appliance control. It uses a 5V~12V TIL control signal which can control DC / AC signal.
  LCD1602-I2C: A standard character display, usually with 2x16 characters. Comes in many colors with LCM1602 IIC attached.
